# Fritzing sketch iotsa-pcb-esp12 (saved by Fritzing 0.9.3b)
circuit board: 6.70848cm x 3.72512cm
breadboards: 3

parts:
  Bare-ESP-12F1 = Bare-ESP-12F
  FTDI = male pin header, 6 pins [form="♂ (male)"]
  PRG = Pushbutton [package="[THT]"]
  RST = Pushbutton [package="[THT]"]
  Pwr_Sel = female pin header, 3 pins [form="♀ (female)"]
  5v = Power Jack [package=power_jack_pth]
  C1 = Tantalum Capacitor [capacitance=10µF voltage=20V package="100 mil [THT, tantalum]"]
  C2 = Tantalum Capacitor [capacitance=10µF voltage=20V package="100 mil [THT, tantalum]"]
  IC1 = Voltage Regulator [package=to-92]
  J9 = female pin header, 7 pins [form="♀ (female)"]
  5v_2 = female pin header, 10 pins [form="♀ (female)"]
  3v3 = female pin header, 10 pins [form="♀ (female)"]
  GND = female pin header, 10 pins [form="♀ (female)"]
  J10 = female pin header, 3 pins [form="♀ (female)"]
  J11 = female pin header, 3 pins [form="♀ (female)"]
  J12 = female pin header, 3 pins [form="♀ (female)"]
  J13 = female pin header, 3 pins [form="♀ (female)"]
  J14 = female pin header, 3 pins [form="♀ (female)"]
  J15 = female pin header, 3 pins [form="♀ (female)"]
  J16 = female pin header, 3 pins [form="♀ (female)"]
  J17 = female pin header, 3 pins [form="♀ (female)"]
  J18 = female pin header, 3 pins [form="♀ (female)"]
  J19 = female pin header, 3 pins [form="♀ (female)"]
  J20 = female pin header, 3 pins [form="♀ (female)"]
  J21 = female pin header, 3 pins [form="♀ (female)"]
  J22 = female pin header, 3 pins [form="♀ (female)"]
  J23 = female pin header, 3 pins [form="♀ (female)"]
  J24 = female pin header, 3 pins [form="♀ (female)"]
  J25 = female pin header, 3 pins [form="♀ (female)"]
  J26 = female pin header, 3 pins [form="♀ (female)"]
  J27 = female pin header, 3 pins [form="♀ (female)"]
  J28 = female pin header, 3 pins [form="♀ (female)"]
  J29 = female pin header, 3 pins [form="♀ (female)"]
  J30 = female pin header, 3 pins [form="♀ (female)"]
  J31 = female pin header, 3 pins [form="♀ (female)"]
  J32 = female pin header, 3 pins [form="♀ (female)"]
  J33 = female pin header, 3 pins [form="♀ (female)"]
  J34 = female pin header, 3 pins [form="♀ (female)"]
  J35 = female pin header, 3 pins [form="♀ (female)"]
  J36 = female pin header, 3 pins [form="♀ (female)"]
  J37 = female pin header, 3 pins [form="♀ (female)"]
  J38 = female pin header, 3 pins [form="♀ (female)"]
  J39 = female pin header, 3 pins [form="♀ (female)"]

nets:
  N1: Bare-ESP-12F1.REST, RST.Pin_1, RST.Pin_2
  N2: Bare-ESP-12F1.ADC, J9.pin3
  3.3V: Bare-ESP-12F1.CH_PD, Bare-ESP-12F1.VCC, Bare-ESP-12F1.GPIO2, Pwr_Sel.pin2, 3v3.pin1, 3v3.pin2, 3v3.pin3, 3v3.pin4, 3v3.pin5, 3v3.pin6, 3v3.pin7, 3v3.pin8, 3v3.pin9, 3v3.pin10
  N3: Bare-ESP-12F1.GPIO16, J9.pin4
  N4: Bare-ESP-12F1.GPIO14, J9.pin5
  N5: Bare-ESP-12F1.GPIO12, J9.pin6
  N6: Bare-ESP-12F1.GPIO13, J9.pin7
  GND: Bare-ESP-12F1.GND, Bare-ESP-12F1.GPIO15, FTDI.pin6, PRG.Pin_3, PRG.Pin_4, RST.Pin_3, RST.Pin_4, 5v.GND, C1.-, C2.-, IC1.GND, GND.pin1, GND.pin2, GND.pin3, GND.pin4, GND.pin5, GND.pin6, GND.pin7, GND.pin8, GND.pin9, GND.pin10
  N7: Bare-ESP-12F1.GPIO0, PRG.Pin_1, PRG.Pin_2
  N8: Bare-ESP-12F1.GPIO4, J9.pin1
  N9: Bare-ESP-12F1.GPIO5, J9.pin2
  N10: Bare-ESP-12F1.RXD, FTDI.pin2
  N11: Bare-ESP-12F1.TXD, FTDI.pin3
  N12: FTDI.pin4, Pwr_Sel.pin1
  N13: Pwr_Sel.pin3, C2.+, IC1.OUT
  5V: 5v.PWR, C1.+, IC1.IN, 5v_2.pin1, 5v_2.pin2, 5v_2.pin3, 5v_2.pin4, 5v_2.pin5, 5v_2.pin6, 5v_2.pin7, 5v_2.pin8, 5v_2.pin9, 5v_2.pin10
  N14: J10.pin1, J10.pin2, J10.pin3
  N15: J11.pin1, J11.pin2, J11.pin3
  N16: J12.pin1, J12.pin2, J12.pin3
  N17: J13.pin1, J13.pin2, J13.pin3
  N18: J14.pin1, J14.pin2, J14.pin3
  N19: J15.pin1, J15.pin2, J15.pin3
  N20: J16.pin1, J16.pin2, J16.pin3
  N21: J17.pin1, J17.pin2, J17.pin3
  N22: J18.pin1, J18.pin2, J18.pin3
  N23: J19.pin1, J19.pin2, J19.pin3
  N24: J20.pin1, J20.pin2, J20.pin3
  N25: J21.pin1, J21.pin2, J21.pin3
  N26: J22.pin1, J22.pin2, J22.pin3
  N27: J23.pin1, J23.pin2, J23.pin3
  N28: J24.pin1, J24.pin2, J24.pin3
  N29: J25.pin1, J25.pin2, J25.pin3
  N30: J26.pin1, J26.pin2, J26.pin3
  N31: J27.pin1, J27.pin2, J27.pin3
  N32: J28.pin1, J28.pin2, J28.pin3
  N33: J29.pin1, J29.pin2, J29.pin3
  N34: J30.pin1, J30.pin2, J30.pin3
  N35: J31.pin1, J31.pin2, J31.pin3
  N36: J32.pin1, J32.pin2, J32.pin3
  N37: J33.pin1, J33.pin2, J33.pin3
  N38: J34.pin1, J34.pin2, J34.pin3
  N39: J35.pin1, J35.pin2, J35.pin3
  N40: J36.pin1, J36.pin2, J36.pin3
  N41: J37.pin1, J37.pin2, J37.pin3
  N42: J38.pin1, J38.pin2, J38.pin3
  N43: J39.pin1, J39.pin2, J39.pin3

notes:
  io5
  gpio5
  io4
  io12
  io13
  io14
  io16
  adc
  Experiment area
  Usable GPIO pins

custom parts:
  Bare-ESP-12F: ESP-12F with minimal breakout board for breadboard use. PCB uses bare ESP-12F.
  Voltage Regulator: Voltage Regulator L78L33 or similar voltage regulator
